# Fritzing sketch toj-apparatus-circuit (saved by Fritzing 0.7.11b)
breadboards: 1

parts:
  R1 = Resistor [tolerance=±5% resistance=1k package=THT]
  R3 = Resistor [tolerance=±5% resistance=10k package=THT]
  S2 = Pushbutton [package="[THT]"]
  R2 = Resistor [tolerance=±5% resistance=1k package=THT]
  Arduino = Arduino
  S1 = Pushbutton [package="[THT]"]
  LED1 = LED - 5mm [color="White (4500K)" package="5 mm [THT]"]
  LED2 = LED - 5mm [color="White (4500K)" package="5 mm [THT]"]

nets:
  N1: R1.Pin_0, Arduino.D12, S1.Pin_1, S1.Pin_2
  N2: R1.Pin_1, R3.Pin_1, R2.Pin_0, Arduino.GND
  N3: R3.Pin_0, LED1.anode, LED2.anode
  N4: S2.Pin_1, S2.Pin_2, S1.Pin_3, S1.Pin_4
  N5: S2.Pin_3, S2.Pin_4, R2.Pin_1, Arduino.D9
  N6: Arduino.D11, LED1.cathode
  N7: Arduino.D10, LED2.cathode
